# Fritzing sketch Buzzer (saved by Fritzing 0.9.3b)
breadboards: 1

parts:
  J1 = Piezo Speaker
  Q1 = NPN-Transistor [package="TO92 [THT]"]
  R1 = Resistor [tolerance=±5% resistance=1k package=THT]
  Bauteil1 = Arduino Uno (Rev3)
  R2 = Resistor [tolerance=±5% resistance=10k package=THT]
  R3 = Resistor [tolerance=±5% resistance=10k package=THT]
  S1 = Pushbutton [package="[THT]"]

nets:
  N1: J1.pin1, Q1.C
  N2: J1.pin2, Bauteil1.5V, R2.Pin_0
  N3: Q1.E, Bauteil1.GND, S1.Pin_3, S1.Pin_4
  N4: Q1.B, R1.Pin_1
  N5: R1.Pin_0, Bauteil1.D9_PWM
  N6: Bauteil1.D12/MISO, R3.Pin_1
  N7: R2.Pin_1, R3.Pin_0, S1.Pin_1, S1.Pin_2
