# Fritzing sketch LEDBar (saved by Fritzing 0.9.3b)
circuit board: 8.46667cm x 5.64444cm
breadboards: 1

parts:
  R1 = Resistor [tolerance=±5% resistance=220 package=THT]
  R2 = Resistor [tolerance=±5% resistance=220 package=THT]
  R3 = Resistor [tolerance=±5% resistance=220 package=THT]
  R4 = Resistor [tolerance=±5% resistance=220 package=THT]
  R5 = Resistor [tolerance=±5% resistance=220 package=THT]
  R6 = Resistor [tolerance=±5% resistance=220 package=THT]
  R7 = Resistor [tolerance=±5% resistance=220 package=THT]
  R8 = Resistor [tolerance=±5% resistance=220 package=THT]
  R9 = Resistor [tolerance=±5% resistance=220 package=THT]
  R10 = Resistor [tolerance=±5% resistance=220 package=THT]
  Bauteil1 = Arduino Uno (Rev3)
  S1 = Pushbutton [package="[THT]"]
  LED_Bar_1 = LED_BARGRAPH_10 [package=led_bargaph_10]
  R11 = Resistor [tolerance=±5% resistance=10k package=THT]
  R12 = Resistor [tolerance=±5% resistance=10k package=THT]
  R13 = Rotary Potentiometer (Small) [maximum_resistance=100kΩ package=THT]

nets:
  N1: R1.Pin_0, R2.Pin_0, R3.Pin_0, R4.Pin_0, R5.Pin_0, R6.Pin_0, R7.Pin_0, R8.Pin_0, R9.Pin_0, R10.Pin_0, Bauteil1.GND, S1.Pin_1, S1.Pin_2, R13.leg1
  N2: R1.Pin_1, LED_Bar_1.A_A
  N3: R2.Pin_1, LED_Bar_1.E_A
  N4: R3.Pin_1, LED_Bar_1.D_A
  N5: R4.Pin_1, LED_Bar_1.I_A
  N6: R5.Pin_1, LED_Bar_1.C_A
  N7: R6.Pin_1, LED_Bar_1.H_A
  N8: R7.Pin_1, LED_Bar_1.B_A
  N9: R8.Pin_1, LED_Bar_1.G_A
  N10: R9.Pin_1, LED_Bar_1.J_A
  N11: R10.Pin_1, LED_Bar_1.F_A
  N12: Bauteil1.A0, R13.wiper
  N13: Bauteil1.D8, LED_Bar_1.G_C
  N14: Bauteil1.D9_PWM, LED_Bar_1.H_C
  N15: Bauteil1.D10_PWM/SS, LED_Bar_1.I_C
  N16: Bauteil1.D11_PWM/MOSI, LED_Bar_1.J_C
  N17: Bauteil1.D12/MISO, R11.Pin_0
  N18: Bauteil1.D2, LED_Bar_1.A_C
  N19: Bauteil1.D3_PWM, LED_Bar_1.B_C
  N20: Bauteil1.D4, LED_Bar_1.C_C
  N21: Bauteil1.D5_PWM, LED_Bar_1.D_C
  N22: Bauteil1.D6_PWM, LED_Bar_1.E_C
  N23: Bauteil1.D7, LED_Bar_1.F_C
  N24: Bauteil1.5V, R12.Pin_0, R13.leg2
  N25: S1.Pin_3, S1.Pin_4, R11.Pin_1, R12.Pin_1
